// Digital circuit Example-Circuit.dig as structural Verilog
module Example_Circuit (
  input  A,
  input  B,
  output Y,
  output Y_2,
  output out_5,
  output out_6
);

  and and_1 (Y, A, B);
  and and_2 (Y_2, A, B);
  or or_1 (out_5, A, B);
  xor xor_1 (out_6, A, B);
endmodule
